# Fritzing sketch minimal-shrimp-blink (saved by Fritzing 0.8.3b)
circuit board: 16.9333cm x 5.64444cm
breadboards: 1

parts:
  U1 = atmega328 [package=dip]
  R1 = Resistor [tolerance=±5% resistance=10k package=THT]
  XTAL1 = Crystal [frequency="16 MHz" package=THT]
  U2 = Embecosm USB to UART [chip_label=USB package="SIP (Single Inline) [THT]"]
  C3 = Ceramic Capacitor [package="100 mil [THT, multilayer]"]
  C2 = Ceramic Capacitor [package="100 mil [THT, multilayer]"]
  C1 = Ceramic Capacitor [package="100 mil [THT, multilayer]"]
  R2 = Resistor [tolerance=±5% resistance=100 package=THT]
  LED1 = LED - 5mm [color="Red (633nm)" package="5 mm [THT]"]

nets:
  N1: U1.RESET, R1.Pin_0, C1.1
  N2: U1.D0_(RX), U2.TXD
  N3: U1.D1_(TX), U2.RXD
  VCC: U1.VCC, U1.AVCC, R1.Pin_1, U2.VCC
  N4: U1.GND#7, U2.GND, C3.0, C2.0
  N5: U1.XLAT1, XTAL1.pin_1, C2.1
  N6: U1.XLAT2, XTAL1.pin_0, C3.1
  N7: U1.D13, LED1.anode
  N8: U1.GND#21, R2.Pin_0
  N9: U2.DTR, C1.0
  N10: R2.Pin_1, LED1.cathode

custom parts:
  Embecosm USB to UART: The Embecosm USB to UART serial port for use with Arduino like devices. 6 inline pins on 0.1in spacing.
  Ceramic Capacitor: 22pF multilayer Ceramic Capacitor
  Ceramic Capacitor: 100 nF multilayer Ceramic Capacitor
