# Fritzing sketch protected-shrimp-blink-battery (saved by Fritzing 0.8.3b)
circuit board: 16.9333cm x 5.64444cm
breadboards: 1

parts:
  U1 = atmega328 [package=dip]
  C1 = Ceramic Capacitor [package="100 mil [THT, multilayer]"]
  C2 = Ceramic Capacitor [package="100 mil [THT, multilayer]"]
  C3 = Ceramic Capacitor [package="100 mil [THT, multilayer]"]
  C4 = Ceramic Capacitor [package="100 mil [THT, multilayer]"]
  S1 = Pushbutton [package="[THT]"]
  R1 = Resistor [tolerance=±5% resistance=10k package=THT]
  D1 = Rectifier Diode [part_number=1N4001 package="300 mil [THT]"]
  XTAL1 = Crystal [frequency="16 MHz" package=THT]
  C5 = Ceramic Capacitor [package="100 mil [THT, multilayer]"]
  C6 = Ceramic Capacitor [package="100 mil [THT, multilayer]"]
  C8 = Electrolytic Capacitor [package="100 mil [THT, electrolytic]"]
  R2 = Resistor [tolerance=±5% resistance=100 package=THT]
  LED1 = LED - 5mm [color="Red (633nm)" package="5 mm [THT]"]
  VCC2 = 3 x AAA Battery Mount

nets (from the breadboard view):
  N1: U1.RESET, U1.GND, C1.1, C2.1, C3.0, S1.Pin_1, S1.Pin_2, S1.Pin_3, S1.Pin_4, R1.Pin_0, D1.anode, C5.0, C6.0, C8.-, R2.Pin_0, VCC2.-
  N2: U1.VCC, U1.AVCC, C2.0, C4.0, R1.Pin_1, D1.cathode, C6.1, C8.+, VCC2.+
  N3: U1.XLAT1, C3.1, C4.1, XTAL1.pin_1
  N4: U1.XLAT2, XTAL1.pin_0
  N5: U1.D13, LED1.anode
  N6: U1.AREF, C5.1
  N7: R2.Pin_1, LED1.cathode

custom parts:
  Ceramic Capacitor: 100 nF multilayer Ceramic Capacitor
  Ceramic Capacitor: 100 nF multilayer Ceramic Capacitor
  Pushbutton: A generic pushbutton.
  Electrolytic Capacitor: A small electrolytic capacitor
  3 x AAA Battery Mount: A 3 x AAA battery pack (4.5 Volts with alkaline batteries)
